# Fritzing sketch lora-receiver (saved by Fritzing 0.9.4)

parts:
  M1 = DOIT Esp32 DevKit v1 (30 pins long, 11 pins width) [part_number=ESP32S-PIN30]
  J1 = Piezo Speaker
  M2 = Osoyoo SX1278-ra-02
  OLED_I2C1 = OLED 128x64 I2C Monochrome Display
  LED1 = LED - 5mm [color="Red (633nm)" package="5 mm [THT]"]
  R1 = Resistor [tolerance=±5% resistance=220 package=THT]
  C1 = Electrolytic Capacitor [capacitance=1µF package="100 mil [THT, electrolytic]"]

nets:
  3V3: M1.3V3, M2.3.3V, OLED_I2C1.VDD
  GND: M1.GND, J1.pin1, M2.GND, OLED_I2C1.GND, LED1.anode, C1.-
  N1: M1.D2, M2.DIO0
  N2: M1.D5, M2.NSS
  N3: M1.D18, M2.SCK
  N4: M1.D19, M2.MISO
  N5: M1.D21, OLED_I2C1.SDA
  N6: M1.D22, OLED_I2C1.SCK
  N7: M1.D23, M2.MOSI
  N8: M1.D14, M2.RST
  N9: M1.D12, J1.pin2
  N10: M1.D13, R1.Pin_0
  N11: M1.VIN, C1.+

custom parts:
  DOIT Esp32 DevKit v1 (30 pins long, 11 pins width): The DOIT Esp32 DevKit v1 is one of the development board created by DOIT to evaluate the ESP-WROOM-32 module. It is based on the ESP32 microcontroller that boasts Wifi, Bluetooth, Ethernet and Low Power support all in a single chip. (vanepp) made breadboard work, adjusted pin numbering and labels and reduced size of schematic and cleaned up pcb. This chip is 30pins long (2 x15) and 11 pins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
  Osoyoo SX1278-ra-02: Osoyoo Long Distance wireless transceiver Uart LoRa Module.
